# Fritzing sketch speedometer (saved by Fritzing 0.9.0b)
circuit board: 8.46667cm x 5.64444cm
breadboards: 1

parts:
  S1 = Reed switch [package=THT]
  S2 = Round Pushbutton
  Part2 = Arduino Micro (Rev3)
  VCC1 = Battery block 9V
  R1 = Resistor [package="0402 [SMD]"]
  U1 = Graphical LCD 128x64 [package=lcd-g12864]
  R2 = Rotary Potentiometer (Small) [maximum_resistance=100kΩ package=THT]

nets:
  N1: S1.pin_1, Part2.5V, U1.E, R2.leg1
  N2: S1.pin_2, R1.Pin_1
  N3: S2.leg0, Part2.GND
  N4: S2.leg1, VCC1.-, R1.Pin_0
  N5: Part2.D2/SDA, U1.CS2
  N6: Part2.D3/SCL, U1.DB7
  N7: Part2.D4_PWM/A6, U1.DB6
  N8: Part2.D5_PWM, U1.DB5
  N9: Part2.D11_PWM, U1.CS1
  N10: Part2.D12_PWM/A11, U1.D_I
  N11: Part2.VIN, VCC1.+
  N12: U1.A, R2.leg2
